// Logisim project regfile.circ as structural Verilog: 1 circuit, main circuit regfile
module regfile (
  input  [4:0] ReadIndex1,
  input  [4:0] ReadIndex2,
  input  [4:0] WriteIndex,
  input  [31:0] WriteData,
  input  RegWEn,
  input  clk,
  output [31:0] ra,
  output [31:0] sp,
  output [31:0] t0,
  output [31:0] t1,
  output [31:0] t2,
  output [31:0] s0,
  output [31:0] s1,
  output [31:0] a0,
  output [31:0] ReadData1,
  output [31:0] ReadData2
);

  wire x0_Input_MUX, x1_Input_MUX, x2_Input_MUX, x3_Input_MUX, x4_Input_MUX, x5_Input_MUX, x6_Input_MUX,
       x7_Input_MUX, x8_Input_MUX, x9_Input_MUX, x10_Input_MUX, x11_Input_MUX, x12_Input_MUX, x13_Input_MUX,
       x14_Input_MUX, x15_Input_MUX, x16_Input_MUX, x17_Input_MUX, x18_Input_MUX, x19_Input_MUX,
       x20_Input_MUX, x21_Input_MUX, x22_Input_MUX, x23_Input_MUX, x24_Input_MUX, x25_Input_MUX,
       x26_Input_MUX, x27_Input_MUX, x28_Input_MUX, x29_Input_MUX, x30_Input_MUX, x31_Input_MUX;
  wire [31:0] a1, a2, a3, a4, a5, a6, a7, gp, multiplexer_3_out, multiplexer_4_out, multiplexer_5_out,
       multiplexer_6_out, multiplexer_7_out, multiplexer_8_out, multiplexer_9_out, multiplexer_10_out,
       multiplexer_11_out, multiplexer_12_out, multiplexer_13_out, multiplexer_14_out, multiplexer_15_out,
       multiplexer_16_out, multiplexer_17_out, multiplexer_18_out, multiplexer_19_out, multiplexer_20_out,
       multiplexer_21_out, multiplexer_22_out, multiplexer_23_out, multiplexer_24_out, multiplexer_25_out,
       multiplexer_26_out, multiplexer_27_out, multiplexer_28_out, multiplexer_29_out, multiplexer_30_out,
       multiplexer_31_out, multiplexer_32_out, multiplexer_33_out, s2, s3, s4, s5, s6, s7, s8, s9, s10, s11,
       t3, t4, t5, t6, tp, zero;

  Decoder #(.select(5)) decoder_1 (
    .out0(x0_Input_MUX), .out1(x1_Input_MUX), .out2(x2_Input_MUX), .out3(x3_Input_MUX), .out4(x4_Input_MUX),
    .out5(x5_Input_MUX), .out6(x6_Input_MUX), .out7(x7_Input_MUX), .out8(x8_Input_MUX), .out9(x9_Input_MUX),
    .out10(x10_Input_MUX), .out11(x11_Input_MUX), .out12(x12_Input_MUX), .out13(x13_Input_MUX),
    .out14(x14_Input_MUX), .out15(x15_Input_MUX), .out16(x16_Input_MUX), .out17(x17_Input_MUX),
    .out18(x18_Input_MUX), .out19(x19_Input_MUX), .out20(x20_Input_MUX), .out21(x21_Input_MUX),
    .out22(x22_Input_MUX), .out23(x23_Input_MUX), .out24(x24_Input_MUX), .out25(x25_Input_MUX),
    .out26(x26_Input_MUX), .out27(x27_Input_MUX), .out28(x28_Input_MUX), .out29(x29_Input_MUX),
    .out30(x30_Input_MUX), .out31(x31_Input_MUX), .sel(WriteIndex));  // open: en
  Multiplexer #(.select(5), .width(32)) multiplexer_1 (
    .in0(zero), .in1(ra), .in2(sp), .in3(gp), .in4(tp), .in5(t0), .in6(t1), .in7(t2), .in8(s0), .in9(s1),
    .in10(a0), .in11(a1), .in12(a2), .in13(a3), .in14(a4), .in15(a5), .in16(a6), .in17(a7), .in18(s2),
    .in19(s3), .in20(s4), .in21(s5), .in22(s6), .in23(s7), .in24(s8), .in25(s9), .in26(s10), .in27(s11),
    .in28(t3), .in29(t4), .in30(t5), .in31(t6), .out(ReadData1), .sel(ReadIndex1));
  Multiplexer #(.select(5), .width(32)) multiplexer_2 (
    .in0(zero), .in1(ra), .in2(sp), .in3(gp), .in4(tp), .in5(t0), .in6(t1), .in7(t2), .in8(s0), .in9(s1),
    .in10(a0), .in11(a1), .in12(a2), .in13(a3), .in14(a4), .in15(a5), .in16(a6), .in17(a7), .in18(s2),
    .in19(s3), .in20(s4), .in21(s5), .in22(s6), .in23(s7), .in24(s8), .in25(s9), .in26(s10), .in27(s11),
    .in28(t3), .in29(t4), .in30(t5), .in31(t6), .out(ReadData2), .sel(ReadIndex2));
  Multiplexer #(.width(32)) multiplexer_3 (.in0(ra), .in1(WriteData), .out(multiplexer_3_out), .sel(x1_Input_MUX));
  Register #(.width(32)) x0 (.D({32{1'b0}}), .en(1'b0), .clk(clk), .Q(zero));  // open: clr
  Register #(.width(32)) x1 (.D(multiplexer_3_out), .en(RegWEn), .clk(clk), .Q(ra));  // open: clr
  Multiplexer #(.width(32)) multiplexer_4 (.in0(sp), .in1(WriteData), .out(multiplexer_4_out), .sel(x2_Input_MUX));
  Register #(.width(32)) x3 (.D(multiplexer_5_out), .en(RegWEn), .clk(clk), .Q(gp));  // open: clr
  Multiplexer #(.width(32)) multiplexer_5 (.in0(gp), .in1(WriteData), .out(multiplexer_5_out), .sel(x3_Input_MUX));
  Register #(.width(32)) x2 (.D(multiplexer_4_out), .en(RegWEn), .clk(clk), .Q(sp));  // open: clr
  Register #(.width(32)) x4 (.D(multiplexer_6_out), .en(RegWEn), .clk(clk), .Q(tp));  // open: clr
  Multiplexer #(.width(32)) multiplexer_6 (.in0(tp), .in1(WriteData), .out(multiplexer_6_out), .sel(x4_Input_MUX));
  Multiplexer #(.width(32)) multiplexer_7 (.in0(t0), .in1(WriteData), .out(multiplexer_7_out), .sel(x5_Input_MUX));
  Multiplexer #(.width(32)) multiplexer_8 (.in0(t1), .in1(WriteData), .out(multiplexer_8_out), .sel(x6_Input_MUX));
  Multiplexer #(.width(32)) multiplexer_9 (.in0(t2), .in1(WriteData), .out(multiplexer_9_out), .sel(x7_Input_MUX));
  Register #(.width(32)) x5 (.D(multiplexer_7_out), .en(RegWEn), .clk(clk), .Q(t0));  // open: clr
  Register #(.width(32)) x6 (.D(multiplexer_8_out), .en(RegWEn), .clk(clk), .Q(t1));  // open: clr
  Register #(.width(32)) x7 (.D(multiplexer_9_out), .en(RegWEn), .clk(clk), .Q(t2));  // open: clr
  Multiplexer #(.width(32)) multiplexer_10 (.in0(s0), .in1(WriteData), .out(multiplexer_10_out), .sel(x8_Input_MUX));
  Multiplexer #(.width(32)) multiplexer_11 (.in0(s1), .in1(WriteData), .out(multiplexer_11_out), .sel(x9_Input_MUX));
  Multiplexer #(.width(32)) multiplexer_12 (.in0(a0), .in1(WriteData), .out(multiplexer_12_out), .sel(x10_Input_MUX));
  Multiplexer #(.width(32)) multiplexer_13 (.in0(a1), .in1(WriteData), .out(multiplexer_13_out), .sel(x11_Input_MUX));
  Register #(.width(32)) x8 (.D(multiplexer_10_out), .en(RegWEn), .clk(clk), .Q(s0));  // open: clr
  Register #(.width(32)) x9 (.D(multiplexer_11_out), .en(RegWEn), .clk(clk), .Q(s1));  // open: clr
  Register #(.width(32)) x10 (.D(multiplexer_12_out), .en(RegWEn), .clk(clk), .Q(a0));  // open: clr
  Register #(.width(32)) x11 (.D(multiplexer_13_out), .en(RegWEn), .clk(clk), .Q(a1));  // open: clr
  Multiplexer #(.width(32)) multiplexer_14 (.in0(a2), .in1(WriteData), .out(multiplexer_14_out), .sel(x12_Input_MUX));
  Multiplexer #(.width(32)) multiplexer_15 (.in0(a3), .in1(WriteData), .out(multiplexer_15_out), .sel(x13_Input_MUX));
  Multiplexer #(.width(32)) multiplexer_16 (.in0(a4), .in1(WriteData), .out(multiplexer_16_out), .sel(x14_Input_MUX));
  Multiplexer #(.width(32)) multiplexer_17 (.in0(a5), .in1(WriteData), .out(multiplexer_17_out), .sel(x15_Input_MUX));
  Register #(.width(32)) x12 (.D(multiplexer_14_out), .en(RegWEn), .clk(clk), .Q(a2));  // open: clr
  Register #(.width(32)) x13 (.D(multiplexer_15_out), .en(RegWEn), .clk(clk), .Q(a3));  // open: clr
  Register #(.width(32)) x14 (.D(multiplexer_16_out), .en(RegWEn), .clk(clk), .Q(a4));  // open: clr
  Register #(.width(32)) x15 (.D(multiplexer_17_out), .en(RegWEn), .clk(clk), .Q(a5));  // open: clr
  Multiplexer #(.width(32)) multiplexer_18 (.in0(a6), .in1(WriteData), .out(multiplexer_18_out), .sel(x16_Input_MUX));
  Multiplexer #(.width(32)) multiplexer_19 (.in0(a7), .in1(WriteData), .out(multiplexer_19_out), .sel(x17_Input_MUX));
  Multiplexer #(.width(32)) multiplexer_20 (.in0(s2), .in1(WriteData), .out(multiplexer_20_out), .sel(x18_Input_MUX));
  Register #(.width(32)) x16 (.D(multiplexer_18_out), .en(RegWEn), .clk(clk), .Q(a6));  // open: clr
  Register #(.width(32)) x17 (.D(multiplexer_19_out), .en(RegWEn), .clk(clk), .Q(a7));  // open: clr
  Register #(.width(32)) x18 (.D(multiplexer_20_out), .en(RegWEn), .clk(clk), .Q(s2));  // open: clr
  Register #(.width(32)) x19 (.D(multiplexer_21_out), .en(RegWEn), .clk(clk), .Q(s3));  // open: clr
  Multiplexer #(.width(32)) multiplexer_21 (.in0(s3), .in1(WriteData), .out(multiplexer_21_out), .sel(x19_Input_MUX));
  Multiplexer #(.width(32)) multiplexer_22 (.in0(s4), .in1(WriteData), .out(multiplexer_22_out), .sel(x20_Input_MUX));
  Register #(.width(32)) x20 (.D(multiplexer_22_out), .en(RegWEn), .clk(clk), .Q(s4));  // open: clr
  Register #(.width(32)) x21 (.D(multiplexer_23_out), .en(RegWEn), .clk(clk), .Q(s5));  // open: clr
  Multiplexer #(.width(32)) multiplexer_23 (.in0(s5), .in1(WriteData), .out(multiplexer_23_out), .sel(x21_Input_MUX));
  Register #(.width(32)) x22 (.D(multiplexer_24_out), .en(RegWEn), .clk(clk), .Q(s6));  // open: clr
  Multiplexer #(.width(32)) multiplexer_24 (.in0(s6), .in1(WriteData), .out(multiplexer_24_out), .sel(x22_Input_MUX));
  Register #(.width(32)) x23 (.D(multiplexer_25_out), .en(RegWEn), .clk(clk), .Q(s7));  // open: clr
  Multiplexer #(.width(32)) multiplexer_25 (.in0(s7), .in1(WriteData), .out(multiplexer_25_out), .sel(x23_Input_MUX));
  Register #(.width(32)) x24 (.D(multiplexer_26_out), .en(RegWEn), .clk(clk), .Q(s8));  // open: clr
  Multiplexer #(.width(32)) multiplexer_26 (.in0(s8), .in1(WriteData), .out(multiplexer_26_out), .sel(x24_Input_MUX));
  Multiplexer #(.width(32)) multiplexer_27 (.in0(s9), .in1(WriteData), .out(multiplexer_27_out), .sel(x25_Input_MUX));
  Register #(.width(32)) x26 (.D(multiplexer_28_out), .en(RegWEn), .clk(clk), .Q(s10));  // open: clr
  Multiplexer #(.width(32)) multiplexer_28 (.in0(s10), .in1(WriteData), .out(multiplexer_28_out), .sel(x26_Input_MUX));
  Register #(.width(32)) x27 (.D(multiplexer_29_out), .en(RegWEn), .clk(clk), .Q(s11));  // open: clr
  Multiplexer #(.width(32)) multiplexer_29 (.in0(s11), .in1(WriteData), .out(multiplexer_29_out), .sel(x27_Input_MUX));
  Register #(.width(32)) x25 (.D(multiplexer_27_out), .en(RegWEn), .clk(clk), .Q(s9));  // open: clr
  Multiplexer #(.width(32)) multiplexer_30 (.in0(t3), .in1(WriteData), .out(multiplexer_30_out), .sel(x28_Input_MUX));
  Multiplexer #(.width(32)) multiplexer_31 (.in0(t4), .in1(WriteData), .out(multiplexer_31_out), .sel(x29_Input_MUX));
  Multiplexer #(.width(32)) multiplexer_32 (.in0(t5), .in1(WriteData), .out(multiplexer_32_out), .sel(x30_Input_MUX));
  Multiplexer #(.width(32)) multiplexer_33 (.in0(t6), .in1(WriteData), .out(multiplexer_33_out), .sel(x31_Input_MUX));
  Register #(.width(32)) x28 (.D(multiplexer_30_out), .en(RegWEn), .clk(clk), .Q(t3));  // open: clr
  Register #(.width(32)) x29 (.D(multiplexer_31_out), .en(RegWEn), .clk(clk), .Q(t4));  // open: clr
  Register #(.width(32)) x30 (.D(multiplexer_32_out), .en(RegWEn), .clk(clk), .Q(t5));  // open: clr
  Register #(.width(32)) x31 (.D(multiplexer_33_out), .en(RegWEn), .clk(clk), .Q(t6));  // open: clr

  // Notes on the sheet:
  //   INPUTS to your circuit
  //   DON'T CHANGE THE LOCATIONS OF THE INPUTS AND OUTPUTS!
  //   These are DEBUG/TEST outputs from your circuit.
  //   OUTPUTS from your circuit
endmodule
